// Digital circuit part_c.dig as structural Verilog
module part_c (
  input  in_0,
  input  in_1,
  input  in_2,
  output out_0
);

  wire in0_bar, in2_bar, N3_s, N5_s, N6_s, P3_d;

  PFET P1 (.G(in_0), .S(1'b1), .D(in0_bar));
  NFET N1 (.G(in_0), .D(in0_bar), .S(1'b0));
  PFET P2 (.G(in_2), .S(1'b1), .D(in2_bar));
  NFET N2 (.G(in_2), .D(in2_bar), .S(1'b0));
  PFET P3 (.G(in0_bar), .S(1'b1), .D(P3_d));
  PFET P5 (.G(in_0), .S(P3_d), .D(out_0));
  NFET N3 (.G(in0_bar), .D(out_0), .S(N3_s));
  NFET N4 (.G(in_2), .D(N3_s), .S(1'b0));
  PFET P6 (.G(in_1), .S(P3_d), .D(out_0));
  PFET P4 (.G(in_2), .S(1'b1), .D(P3_d));
  PFET P7 (.G(in2_bar), .S(P3_d), .D(out_0));
  NFET N5 (.G(in_0), .D(out_0), .S(N5_s));
  NFET N6 (.G(in_1), .D(N5_s), .S(N6_s));
  NFET N7 (.G(in2_bar), .D(N6_s), .S(1'b0));

  // Other names for the same wires on the sheet: in0 = in_0; in1 = in_1; in2 = in_2
endmodule

/* Test case part_c_test:
in_0 in_1 in_2 out_0 

 0 0 0 1
 0 0 1 0
 0 1 0 1
 0 1 1 0
 1 0 0 1
 1 0 1 1
 1 1 0 0
 1 1 1 1
*/
